// Logisim project BDEProject2.circ as structural Verilog: 7 circuits, main circuit main
module main (
);

  wire alu_1_z, and_1_out, clock_1_out, control_1_alusrc, control_1_cbr, control_1_flagset,
       control_1_mem2reg, control_1_memread, control_1_memwrite, control_1_regwrite, control_1_ubr, or_1_out;
  wire [2:0] control_1_aluaction;
  wire [3:0] alu_1_aluout;
  wire [4:0] instructionmem_1_rd, instructionmem_1_rm, instructionmem_1_rn, multiplexer_3_out;
  wire [7:0] adder_1_out, bit_extender_2_out, multiplexer_2_out, pc_1_addressout;
  wire [9:0] bit_extender_3_out;
  wire [10:0] instructionmem_1_imm11, instructionmem_1_opcode;
  wire [27:0] alu_1_aluout_2;
  wire [31:0] bit_extender_1_out, bit_extender_4_out, datamem_1_readdatam, multiplexer_1_out,
       multiplexer_4_out, multiplexer_5_out, regfile_1_regdata1, regfile_1_regdata2;

  and and_1 (and_1_out, control_1_cbr, alu_1_z);
  Clock #(.highDuration(2), .lowDuration(2)) clock_1 (.out(clock_1_out));
  Adder adder_1 (.a(pc_1_addressout), .b(8'h1), .out(adder_1_out));  // open: cin, cout
  or or_1 (or_1_out, control_1_ubr, and_1_out);
  assign bit_extender_1_out = {{24{pc_1_addressout[7]}}, pc_1_addressout};  // Bit_Extender bit_extender_1
  Multiplexer #(.width(32)) multiplexer_1 (
    .in0(regfile_1_regdata1), .in1(bit_extender_1_out), .out(multiplexer_1_out), .sel(or_1_out));
  Multiplexer #(.width(8)) multiplexer_2 (
    .in0(adder_1_out), .in1(bit_extender_2_out), .out(multiplexer_2_out), .sel(or_1_out));
  Multiplexer #(.width(5)) multiplexer_3 (
    .in0(instructionmem_1_rn), .in1(instructionmem_1_rd), .out(multiplexer_3_out), .sel(control_1_memwrite));
  PC pc_1 (.Address(multiplexer_2_out), .Clock(clock_1_out), .AddressOut(pc_1_addressout));
  RegFile regfile_1 (
    .RegDataW(multiplexer_5_out), .RegWrite(control_1_regwrite), .CLK(clock_1_out),
    .WriteReg(instructionmem_1_rd), .ReadReg1(instructionmem_1_rm), .ReadReg2(multiplexer_3_out),
    .RegData1(regfile_1_regdata1), .RegData2(regfile_1_regdata2));
  InstructionMem instructionmem_1 (
    .Address(pc_1_addressout), .Clock(clock_1_out), .imm11(instructionmem_1_imm11),
    .Opcode(instructionmem_1_opcode), .Rn(instructionmem_1_rn), .Rm(instructionmem_1_rm),
    .Rd(instructionmem_1_rd));
  Bit_Extender #(.in_width(32), .out_width(8)) bit_extender_2 (
    .in({alu_1_aluout_2, alu_1_aluout}), .out(bit_extender_2_out));
  Bit_Extender #(.in_width(32), .out_width(10)) bit_extender_3 (
    .in({alu_1_aluout_2, alu_1_aluout}), .out(bit_extender_3_out));
  assign bit_extender_4_out = {{21{instructionmem_1_imm11[10]}}, instructionmem_1_imm11};  // Bit_Extender bit_extender_4
  Control control_1 (
    .Opcode(instructionmem_1_opcode), .MemWrite(control_1_memwrite), .MemRead(control_1_memread),
    .RegWrite(control_1_regwrite), .UBr(control_1_ubr), .ALUSrc(control_1_alusrc),
    .ALUAction(control_1_aluaction), .FlagSet(control_1_flagset), .Mem2Reg(control_1_mem2reg),
    .CBr(control_1_cbr));
  Multiplexer #(.width(32)) multiplexer_4 (
    .in0(regfile_1_regdata2), .in1(bit_extender_4_out), .out(multiplexer_4_out), .sel(control_1_alusrc));
  ALU alu_1 (
    .Input1(multiplexer_1_out), .Input2(multiplexer_4_out), .ALUAction(control_1_aluaction),
    .FlagSet(clock_1_out), .Clock(control_1_flagset), .ALUOut({alu_1_aluout_2, alu_1_aluout}), .Z(alu_1_z));
  DataMem datamem_1 (
    .Address(bit_extender_3_out), .MemRead(control_1_memread), .MemWrite(control_1_memwrite),
    .WriteDataM(regfile_1_regdata2), .ReadDataM(datamem_1_readdatam));
  Multiplexer #(.width(32)) multiplexer_5 (
    .in0({alu_1_aluout_2, alu_1_aluout}), .in1(datamem_1_readdatam), .out(multiplexer_5_out),
    .sel(control_1_mem2reg));
  Hex_Digit_Display LED (.value(alu_1_aluout));  // open: dp

  // Notes on the sheet:
  //   Justin Kamal
  //   I pledge my honor that I have abided by the Stevens Honors System
  //   CPU Name: BDE (Big Data Energy)
endmodule

// RegisterFile
module RegFile (
  input  [31:0] RegDataW,
  input  RegWrite,
  input  CLK,
  input  [4:0] WriteReg,
  input  [4:0] ReadReg1,
  input  [4:0] ReadReg2,
  output [31:0] RegData1,
  output [31:0] RegData2
);

  wire and_1_out, and_2_out, and_3_out, and_4_out, and_5_out, and_6_out, and_7_out, and_8_out, and_9_out,
       and_10_out, and_11_out, and_12_out, and_13_out, and_14_out, and_15_out, and_16_out, and_17_out,
       and_18_out, and_19_out, and_20_out, and_21_out, and_22_out, and_23_out, and_24_out, and_25_out,
       and_26_out, and_27_out, and_28_out, and_29_out, and_30_out, and_31_out, and_32_out;
  wire [7:0] decoder_1_out0, decoder_1_out8, decoder_1_out16, decoder_1_out24;
  wire [31:0] register_1_q, register_2_q, register_3_q, register_4_q, register_5_q, register_6_q,
       register_7_q, register_8_q, register_9_q, register_10_q, register_11_q, register_12_q, register_13_q,
       register_14_q, register_15_q, register_16_q, register_17_q, register_18_q, register_19_q,
       register_20_q, register_21_q, register_22_q, register_23_q, register_24_q, register_25_q,
       register_26_q, register_27_q, register_28_q, register_29_q, register_30_q, register_31_q,
       register_32_q;

  Decoder #(.select(5)) decoder_1 (
    .out0(decoder_1_out0[0]), .out1(decoder_1_out0[1]), .out2(decoder_1_out0[2]), .out3(decoder_1_out0[3]),
    .out4(decoder_1_out0[4]), .out5(decoder_1_out0[5]), .out6(decoder_1_out0[6]), .out7(decoder_1_out0[7]),
    .out8(decoder_1_out8[0]), .out9(decoder_1_out8[1]), .out10(decoder_1_out8[2]), .out11(decoder_1_out8[3]),
    .out12(decoder_1_out8[4]), .out13(decoder_1_out8[5]), .out14(decoder_1_out8[6]),
    .out15(decoder_1_out8[7]), .out16(decoder_1_out16[0]), .out17(decoder_1_out16[1]),
    .out18(decoder_1_out16[2]), .out19(decoder_1_out16[3]), .out20(decoder_1_out16[4]),
    .out21(decoder_1_out16[5]), .out22(decoder_1_out16[6]), .out23(decoder_1_out16[7]),
    .out24(decoder_1_out24[0]), .out25(decoder_1_out24[1]), .out26(decoder_1_out24[2]),
    .out27(decoder_1_out24[3]), .out28(decoder_1_out24[4]), .out29(decoder_1_out24[5]),
    .out30(decoder_1_out24[6]), .out31(decoder_1_out24[7]), .sel(WriteReg), .en(1'b1));
  and and_1 (and_1_out, RegWrite, decoder_1_out0[0]);
  and and_2 (and_2_out, RegWrite, decoder_1_out0[1]);
  and and_3 (and_3_out, RegWrite, decoder_1_out0[2]);
  and and_4 (and_4_out, RegWrite, decoder_1_out0[3]);
  and and_5 (and_5_out, RegWrite, decoder_1_out0[4]);
  and and_6 (and_6_out, RegWrite, decoder_1_out0[5]);
  and and_7 (and_7_out, RegWrite, decoder_1_out0[6]);
  and and_8 (and_8_out, RegWrite, decoder_1_out0[7]);
  and and_9 (and_9_out, RegWrite, decoder_1_out8[0]);
  and and_10 (and_10_out, RegWrite, decoder_1_out8[1]);
  and and_11 (and_11_out, RegWrite, decoder_1_out8[2]);
  and and_12 (and_12_out, RegWrite, decoder_1_out8[3]);
  and and_13 (and_13_out, RegWrite, decoder_1_out8[4]);
  and and_14 (and_14_out, RegWrite, decoder_1_out8[5]);
  and and_15 (and_15_out, RegWrite, decoder_1_out8[6]);
  and and_16 (and_16_out, RegWrite, decoder_1_out8[7]);
  Register #(.width(32)) register_1 (.D(RegDataW), .en(and_1_out), .clk(CLK), .Q(register_1_q), .clr(1'b0));
  Register #(.width(32)) register_2 (.D(RegDataW), .en(and_2_out), .clk(CLK), .Q(register_2_q), .clr(1'b0));
  Register #(.width(32)) register_3 (.D(RegDataW), .en(and_3_out), .clk(CLK), .Q(register_3_q), .clr(1'b0));
  Register #(.width(32)) register_4 (.D(RegDataW), .en(and_4_out), .clk(CLK), .Q(register_4_q), .clr(1'b0));
  Register #(.width(32)) register_5 (.D(RegDataW), .en(and_5_out), .clk(CLK), .Q(register_5_q), .clr(1'b0));
  Register #(.width(32)) register_6 (.D(RegDataW), .en(and_6_out), .clk(CLK), .Q(register_6_q), .clr(1'b0));
  Register #(.width(32)) register_7 (.D(RegDataW), .en(and_7_out), .clk(CLK), .Q(register_7_q), .clr(1'b0));
  Register #(.width(32)) register_8 (.D(RegDataW), .en(and_8_out), .clk(CLK), .Q(register_8_q), .clr(1'b0));
  Register #(.width(32)) register_9 (.D(RegDataW), .en(and_9_out), .clk(CLK), .Q(register_9_q), .clr(1'b0));
  Register #(.width(32)) register_10 (.D(RegDataW), .en(and_10_out), .clk(CLK), .Q(register_10_q), .clr(1'b0));
  Register #(.width(32)) register_11 (.D(RegDataW), .en(and_11_out), .clk(CLK), .Q(register_11_q), .clr(1'b0));
  Register #(.width(32)) register_12 (.D(RegDataW), .en(and_12_out), .clk(CLK), .Q(register_12_q), .clr(1'b0));
  Register #(.width(32)) register_13 (.D(RegDataW), .en(and_13_out), .clk(CLK), .Q(register_13_q), .clr(1'b0));
  Register #(.width(32)) register_14 (.D(RegDataW), .en(and_14_out), .clk(CLK), .Q(register_14_q), .clr(1'b0));
  Register #(.width(32)) register_15 (.D(RegDataW), .en(and_15_out), .clk(CLK), .Q(register_15_q), .clr(1'b0));
  Register #(.width(32)) register_16 (.D(RegDataW), .en(and_16_out), .clk(CLK), .Q(register_16_q), .clr(1'b0));
  and and_17 (and_17_out, RegWrite, decoder_1_out16[0]);
  and and_18 (and_18_out, RegWrite, decoder_1_out16[1]);
  and and_19 (and_19_out, RegWrite, decoder_1_out16[2]);
  and and_20 (and_20_out, RegWrite, decoder_1_out16[3]);
  and and_21 (and_21_out, RegWrite, decoder_1_out16[4]);
  and and_22 (and_22_out, RegWrite, decoder_1_out16[5]);
  and and_23 (and_23_out, RegWrite, decoder_1_out16[6]);
  and and_24 (and_24_out, RegWrite, decoder_1_out16[7]);
  and and_25 (and_25_out, RegWrite, decoder_1_out24[0]);
  and and_26 (and_26_out, RegWrite, decoder_1_out24[1]);
  and and_27 (and_27_out, RegWrite, decoder_1_out24[2]);
  and and_28 (and_28_out, RegWrite, decoder_1_out24[3]);
  and and_29 (and_29_out, RegWrite, decoder_1_out24[4]);
  and and_30 (and_30_out, RegWrite, decoder_1_out24[5]);
  and and_31 (and_31_out, RegWrite, decoder_1_out24[6]);
  and and_32 (and_32_out, RegWrite, decoder_1_out24[7]);
  Register #(.width(32)) register_17 (.D(RegDataW), .en(and_17_out), .clk(CLK), .Q(register_17_q), .clr(1'b0));
  Register #(.width(32)) register_18 (.D(RegDataW), .en(and_18_out), .clk(CLK), .Q(register_18_q), .clr(1'b0));
  Register #(.width(32)) register_19 (.D(RegDataW), .en(and_19_out), .clk(CLK), .Q(register_19_q), .clr(1'b0));
  Register #(.width(32)) register_20 (.D(RegDataW), .en(and_20_out), .clk(CLK), .Q(register_20_q), .clr(1'b0));
  Register #(.width(32)) register_21 (.D(RegDataW), .en(and_21_out), .clk(CLK), .Q(register_21_q), .clr(1'b0));
  Register #(.width(32)) register_22 (.D(RegDataW), .en(and_22_out), .clk(CLK), .Q(register_22_q), .clr(1'b0));
  Register #(.width(32)) register_23 (.D(RegDataW), .en(and_23_out), .clk(CLK), .Q(register_23_q), .clr(1'b0));
  Register #(.width(32)) register_24 (.D(RegDataW), .en(and_24_out), .clk(CLK), .Q(register_24_q), .clr(1'b0));
  Register #(.width(32)) register_25 (.D(RegDataW), .en(and_25_out), .clk(CLK), .Q(register_25_q), .clr(1'b0));
  Register #(.width(32)) register_26 (.D(RegDataW), .en(and_26_out), .clk(CLK), .Q(register_26_q), .clr(1'b0));
  Register #(.width(32)) register_27 (.D(RegDataW), .en(and_27_out), .clk(CLK), .Q(register_27_q), .clr(1'b0));
  Register #(.width(32)) register_28 (.D(RegDataW), .en(and_28_out), .clk(CLK), .Q(register_28_q), .clr(1'b0));
  Register #(.width(32)) register_29 (.D(RegDataW), .en(and_29_out), .clk(CLK), .Q(register_29_q), .clr(1'b0));
  Register #(.width(32)) register_30 (.D(RegDataW), .en(and_30_out), .clk(CLK), .Q(register_30_q), .clr(1'b0));
  Register #(.width(32)) register_31 (.D(RegDataW), .en(and_31_out), .clk(CLK), .Q(register_31_q), .clr(1'b0));
  Register #(.width(32)) register_32 (.D(RegDataW), .en(and_32_out), .clk(CLK), .Q(register_32_q), .clr(1'b0));
  Multiplexer #(.select(5), .width(32)) multiplexer_1 (
    .in0(register_1_q), .in1(register_2_q), .in2(register_3_q), .in3(register_4_q), .in4(register_5_q),
    .in5(register_6_q), .in6(register_7_q), .in7(register_8_q), .in8(register_9_q), .in9(register_10_q),
    .in10(register_11_q), .in11(register_12_q), .in12(register_13_q), .in13(register_14_q),
    .in14(register_15_q), .in15(register_16_q), .in16(register_17_q), .in17(register_18_q),
    .in18(register_19_q), .in19(register_20_q), .in20(register_21_q), .in21(register_22_q),
    .in22(register_23_q), .in23(register_24_q), .in24(register_25_q), .in25(register_26_q),
    .in26(register_27_q), .in27(register_28_q), .in28(register_29_q), .in29(register_30_q),
    .in30(register_31_q), .in31(register_32_q), .out(RegData1), .sel(ReadReg1));
  Multiplexer #(.select(5), .width(32)) multiplexer_2 (
    .in0(register_1_q), .in1(register_2_q), .in2(register_3_q), .in3(register_4_q), .in4(register_5_q),
    .in5(register_6_q), .in6(register_7_q), .in7(register_8_q), .in8(register_9_q), .in9(register_10_q),
    .in10(register_11_q), .in11(register_12_q), .in12(register_13_q), .in13(register_14_q),
    .in14(register_15_q), .in15(register_16_q), .in16(register_17_q), .in17(register_18_q),
    .in18(register_19_q), .in19(register_20_q), .in20(register_21_q), .in21(register_22_q),
    .in22(register_23_q), .in23(register_24_q), .in24(register_25_q), .in25(register_26_q),
    .in26(register_27_q), .in27(register_28_q), .in28(register_29_q), .in29(register_30_q),
    .in30(register_31_q), .in31(register_32_q), .out(RegData2), .sel(ReadReg2));

  // Notes on the sheet:
  //   RegDataW: pull=down
  //   RegWrite: pull=down
endmodule

module ALU (
  input  [31:0] Input1,
  input  [31:0] Input2,
  input  [2:0] ALUAction,
  input  FlagSet,
  input  Clock,
  output [31:0] ALUOut,
  output Z
);

  wire and_1_out;
  wire [31:0] adder_1_out, multiplier_1_out, subtractor_1_out, xor_1_out;

  Adder #(.width(32)) adder_1 (.a(Input1), .b(Input2), .out(adder_1_out), .cin(1'b0));  // open: cout
  Subtractor #(.width(32)) subtractor_1 (.a(Input1), .b(Input2), .out(subtractor_1_out), .bin(1'b0));  // open: bout
  Multiplier #(.width(32)) multiplier_1 (.a(Input1), .b(Input2), .out(multiplier_1_out));  // open: cin, cout
  assign xor_1_out = subtractor_1_out ^ {32{1'b1}};  // XOR_Gate xor_1, 32 bits wide
  Multiplexer #(.select(3), .width(32)) multiplexer_1 (
    .in0(adder_1_out), .in1(subtractor_1_out), .in2(multiplier_1_out), .out(ALUOut), .sel(ALUAction));  // open: in3, in4, in5, in6, in7
  and and_1 (and_1_out, xor_1_out[15], xor_1_out[0], xor_1_out[1], xor_1_out[2], xor_1_out[3], xor_1_out[4], xor_1_out[5], xor_1_out[6], xor_1_out[7], xor_1_out[8], xor_1_out[9], xor_1_out[10], xor_1_out[11], xor_1_out[12], xor_1_out[13], xor_1_out[14], xor_1_out[16], xor_1_out[17], xor_1_out[18], xor_1_out[19], xor_1_out[20], xor_1_out[21], xor_1_out[22], xor_1_out[23], xor_1_out[24], xor_1_out[25], xor_1_out[26], xor_1_out[27], xor_1_out[28], xor_1_out[29], xor_1_out[30], xor_1_out[31]);
  Register #(.width(1)) register_1 (.D(and_1_out), .en(FlagSet), .clk(Clock), .Q(Z), .clr(1'b0));

  // Notes on the sheet:
  //   ALUAction: pull=down
  //   ALUOut: pull=down
  //   Z: pull=down
  //   Input1: pull=down
  //   Input2: pull=down
  //   FlagSet: pull=down
endmodule

module PC (
  input  [7:0] Address,
  input  Clock,
  output [7:0] AddressOut
);

  wire not_1_out;

  not not_1 (not_1_out, Clock);
  Register register_1 (.D(Address), .en(not_1_out), .clk(not_1_out), .Q(AddressOut), .clr(1'b0));

  // Notes on the sheet:
  //   Clock: pull=down
  //   Address: pull=down
  //   AddressOut: pull=down
endmodule

module Control (
  input  [10:0] Opcode,
  output MemWrite,
  output MemRead,
  output RegWrite,
  output UBr,
  output ALUSrc,
  output [2:0] ALUAction,
  output FlagSet,
  output Mem2Reg,
  output CBr
);


  assign ALUAction = {Opcode[3], Opcode[4], Opcode[5]};
  assign ALUSrc = Opcode[6];
  assign CBr = Opcode[0];
  assign FlagSet = Opcode[2];
  assign Mem2Reg = Opcode[1];
  assign MemRead = Opcode[9];
  assign MemWrite = Opcode[10];
  assign RegWrite = Opcode[8];
  assign UBr = Opcode[7];
endmodule

module DataMem (
  input  [9:0] Address,
  input  MemRead,
  input  MemWrite,
  input  [31:0] WriteDataM,
  output [31:0] ReadDataM
);

  wire clock_1_out;

  Clock clock_1 (.out(clock_1_out));
  RAM #(.addrWidth(10), .dataWidth(32)) ram_1 (
    .addr(Address), .we(MemWrite), .oe(MemRead), .clk(clock_1_out), .din(WriteDataM), .dout(ReadDataM));

  // Notes on the sheet:
  //   MemRead: pull=down
  //   MemWrite: pull=down
  //   Address: pull=down
endmodule

module InstructionMem (
  input  [7:0] Address,
  input  Clock,
  output [10:0] imm11,
  output [10:0] Opcode,
  output [4:0] Rn,
  output [4:0] Rm,
  output [4:0] Rd
);

  RAM #(.dataWidth(32)) Program (
    .addr(Address), .we(1'b0), .oe(1'b1), .clk(Clock), .dout({Opcode, imm11, Rm, Rd}));  // open: din

  assign Rn = imm11[4:0];

  // Notes on the sheet:
  //   Rn: pull=down
  //   imm11: pull=down
endmodule
